# Fritzing sketch DHT11,LED (saved by Fritzing 0.9.4)
breadboards: 1

parts:
  Part1 = Arduino Uno (Rev3)
  LED1 = LED - 5mm [color="Green (560nm)" package="5 mm [THT]"]
  LED2 = LED - 5mm [color="Green (560nm)" package="5 mm [THT]"]
  R1 = Resistor [tolerance=±5% resistance=180 package=THT]
  R2 = Resistor [tolerance=±5% resistance=180 package=THT]
  RHT1 = Humidity and Temperature Sensor RHT03
  R3 = Resistor [tolerance=±5% resistance=4.7k package=THT]

nets:
  N1: Part1.D8, LED1.cathode
  N2: Part1.D9_PWM, LED2.cathode
  N3: Part1.GND, R1.Pin_1, R2.Pin_1
  N4: Part1.D2, RHT1.Data-signal, R3.Pin_1
  N5: Part1.3V3, RHT1.GND_2
  5V: Part1.5V, RHT1.Vcc, R3.Pin_0
  N6: LED1.anode, R1.Pin_0
  N7: LED2.anode, R2.Pin_0
